# Fritzing sketch laserFotoLed (saved by Fritzing 0.9.1b)
breadboards: 1

parts:
  Arduino = Arduino Uno (Rev3)
  R1 = Resistor [tolerance=±5% resistance=220 package="1206 [SMD]"]
  LED1 = smd LED [color="Red (633nm)" package="0603 [SMD]"]
  Fotoresistencia = PHOTOCELL [package=photocell-kit]
  R3 = Resistor [tolerance=±20% resistance=10k package="1206 [SMD]"]

nets:
  N1: Arduino.A0, Fotoresistencia.P$2, R3.Pin_0
  N2: Arduino.GND, LED1.cathode, Fotoresistencia.P$1
  N3: Arduino.D7, R1.Pin_1
  N4: Arduino.5V, R3.Pin_1
  N5: R1.Pin_0, LED1.anode
