# Fritzing sketch one_digit_counter_schema (saved by Fritzing 0.9.2b)
breadboards: 1

parts:
  Part1 = Arduino Uno (Rev3) - ICSP
  R1 = Resistor [tolerance=±5% resistance=330 package="2512 [SMD]"]
  R2 = Resistor [tolerance=±5% resistance=15k package=THT]
  C1 = Electrolytic Capacitor [capacitance=10μF voltage=50V package="0605 [SMD, electrolytic]"]
  S1 = SWITCH-MOMENTARY-2 [package=tactile-pth-12mm]
  7_Segment1 = 7 Segment Display

nets:
  N1: Part1.5V, R1.Pin_0, S1.2
  GND: Part1.GND, R2.Pin_1, C1.-
  N2: Part1.D8, 7_Segment1.Segment_G
  N3: Part1.D9_PWM, R2.Pin_0, C1.+, S1.1
  N4: Part1.D2, 7_Segment1.Segment_A
  N5: Part1.D3_PWM, 7_Segment1.Segment_B
  N6: Part1.D4, 7_Segment1.Segment_C
  N7: Part1.D5_PWM, 7_Segment1.Segment_D
  N8: Part1.D6_PWM, 7_Segment1.Segment_E
  N9: Part1.D7, 7_Segment1.Segment_F
